# Fritzing sketch fritzing (saved by Fritzing 1.0.3b)
breadboards: 2

parts:
  Mod1 = Raspberry Pi 4B
  Power_plug1 = Power plug
  8x8_LED_Modul_mit_MAX1 = 8x8 LED Modul mit MAX7219 [package=THT]
  New_Part2 = MCP23017 [package="DIP (Dual Inline) [THT]"]
  Q2 = NPN-Transistor [package="TO92 [THT]"]
  R1 = Resistor [tolerance=±5% resistance=1k power=0W package="0402 [SMD]"]
  R2 = Resistor [tolerance=±5% resistance=1k package="0402 [SMD]"]
  LED1 = smd LED [color="Blue (470nm)" package="0805 [SMD]"]

nets:
  N1: Mod1.GPIO2, New_Part2.SCL
  N2: Mod1.GPIO3, New_Part2.SDA
  GND: Mod1.GND, Power_plug1.GND, New_Part2.GND, New_Part2.A0, New_Part2.A1, New_Part2.A2, LED1.cathode
  VCC: Power_plug1.VCC, 8x8_LED_Modul_mit_MAX1.VCC_Eingang, New_Part2.VCC, New_Part2.RST, Q2.C, R1.Pin_0, R2.Pin_0
  N3: Q2.B, R1.Pin_1
  N4: R2.Pin_1, LED1.anode

notes:
  5V
  Here a 8x 7 segment module
  https://www.az-delivery.de/products/azdelivery-max7219-led-modul-8-bit-7-segmentanzeige-led-display-fur-arduino-und-raspberry-pi

custom parts:
  MCP23017: 16 bit I/O chip controlled via I2C
